# Fritzing sketch Project 1 (saved by Fritzing 0.9.4)
breadboards: 1

parts:
  U1 = TCRT5000 [package=THT]
  U2 = TCRT5000 [package=THT]
  U3 = TCRT5000 [package=THT]
  R6 = Resistor [tolerance=±5% resistance=100 package="0402 [SMD]"]
  R7 = Resistor [tolerance=±5% resistance=100 package="0402 [SMD]"]
  R8 = Resistor [tolerance=±5% resistance=100 package="0402 [SMD]"]
  R10 = Resistor [tolerance=±5% resistance=10k package="0402 [SMD]"]
  R13 = Resistor [tolerance=±5% resistance=10k package="0402 [SMD]"]
  R14 = Resistor [tolerance=±5% resistance=10k package="0402 [SMD]"]
  Part1 = Adafruit 1.44 inch TFT Breakout [part_number="Adafruit #2088"]
  Raspberry_Pi_1 = Raspberry Pi 3 [part_number=RPI-3-V1.2]  # not connected
  M2 = DC Motor
  Part2 = Adafruit DC+Stepper Motor HAT [part_number="Adafruit #2348"]
  M3 = DC Motor
  BAT1 = Battery Holders [package=battery-aa]
  BAT2 = Battery Holders [package=battery-aa]
  BAT3 = Battery Holders [package=battery-aa]
  BAT4 = Battery Holders [package=battery-aa]
  BAT5 = Battery Holders [package=battery-aa]
  U4 = TCM8240MD [package=tcm8240md]  # not connected

nets:
  GND: U1.Pin_1, U1.Pin_2, U1.Pin_3, U1.Pin_4, U2.Pin_1, U2.Pin_2, U2.Pin_3, U2.Pin_4, U3.Pin_1, U3.Pin_2, U3.Pin_3, U3.Pin_4, R6.Pin_1, R7.Pin_1, R8.Pin_1, R10.Pin_1, R13.Pin_1, R14.Pin_1, Part1.GND, Part2.GND, Part2.GPIO13, Part2.GPIO19, Part2.GPIO26, BAT1.+
  VIN: R6.Pin_0, R7.Pin_0, R8.Pin_0, R10.Pin_0, R13.Pin_0, R14.Pin_0, Part1.VIN, Part2.3.3V
  N1: Part1.SCK, Part2.SPI_SCLK
  N2: Part1.MOSI, Part2.SPI_MOSI
  N3: Part1.TFTCS, Part2.SPI_CE0
  N4: Part1.RESET, Part2.GPIO24
  N5: Part1.TFTDC, Part2.GPIO25
  N6: M2.pin_1, Part2.M1B
  N7: M2.pin_2, Part2.M1A
  N8: Part2.M2A, M3.pin_1
  N9: Part2.M2B, M3.pin_2
  N10: Part2.VMOTOR, BAT5.-
  N11: BAT1.-, BAT2.+
  N12: BAT2.-, BAT3.+
  N13: BAT3.-, BAT4.+
  N14: BAT4.-, BAT5.+

notes:
  The yellow wire is to show the camera connection to the PI
  On the robot the LCD and sensor are on two seperate breadboards. To save space it is on one in the Fritzing

custom parts:
  TCRT5000: TCRT5000 optical reflective sensor
  Adafruit 1.44 inch TFT Breakout: This lovely little display breakout is the best way to add a small, colorful and bright display to any project. Since the display uses 4-wire SPI to communicate and has its own pixel-addressable frame buffer, it can be used with every kind of microcontroller. Even a very small one with low memory and few pins available! The 1.44" display has 128x128 color pixels. Unlike the low cost "Nokia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
  Adafruit DC+Stepper Motor HAT: Let your robotic dreams come true with the new DC+Stepper Motor HAT from Adafruit. This Raspberry Pi add-on is perfect for any motion project as it can drive up to 4 DC or 2 Stepper motors with full PWM speed control. Since the Raspberry Pi does not have a lot of PWM pins, we use a fully-dedicated PWM driver chip onboard to both control motor direction and speed. This chip handles all the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
